# Fritzing sketch HDD-Clicker-Mark-00 (saved by Fritzing 0.9.3b)
breadboards: 1

parts:
  C1 = Ceramic Capacitor [capacitance=100nF package="100 mil [THT, multilayer]"]
  buz1 = Piezo Buzzer
  J2 = male pin header, 2 pins [form="♂ (male)"]
  J1 = male pin header, 2 pins [form="♂ (male)"]

nets:
  N1: C1.0, buz1.pin_2, J2.pin1, J1.pin1
  N2: C1.1, buz1.pin_1, J2.pin2, J1.pin2

notes:
  +
  -

custom parts:
  Piezo Buzzer: Part from https://www.nutsvolts.com/magazine/article/november2012_SmileysWorkshop. Breadboard and icon images modified to be 0.3" in spacing and be more similar to the actual physical part.
