# Fritzing sketch HDD-Clicker-Mark-01 (saved by Fritzing 0.9.3b)
breadboards: 1

parts:
  C1 = Ceramic Capacitor [capacitance=100nF package="100 mil [THT, multilayer]"]
  J1 = male pin header, 2 pins [form="♂ (male)"]
  J2 = male pin header, 2 pins [form="♂ (male)"]
  buz1 = Piezo Buzzer
  J5 = male pin header, 4 pins [form="♂ (male)"]
  R1 = Resistor [tolerance=±5% resistance=220 package=THT]
  R2 = Resistor [tolerance=±5% resistance=15k package=THT]
  LED1 = LED - 5mm [color="Red (633nm)" package="5 mm [THT]"]
  Q1 = TRANSISTOR_NPN [package=to-92-ammo]

nets:
  N1: C1.0, J1.pin1, J2.pin1, Q1.E
  N2: C1.1, J1.pin2, J2.pin2, R2.Pin_0
  N3: buz1.pin_1, J5.pin4, LED1.anode
  N4: buz1.pin_2, R1.Pin_1, Q1.C
  N5: R1.Pin_0, LED1.cathode
  N6: R2.Pin_1, Q1.B

notes:
  +5V
  EBC
  +
  -

custom parts:
  Piezo Buzzer: Part from https://www.nutsvolts.com/magazine/article/november2012_SmileysWorkshop. Breadboard and icon images modified to be 0.3" in spacing and be more similar to the actual physical part.
