# Fritzing sketch HDD-Clicker-Mark-02 (saved by Fritzing 0.9.3b)
breadboards: 1

parts:
  C2 = Ceramic Capacitor [capacitance=100nF package="100 mil [THT, multilayer]"]
  J6 = male pin header, 2 pins [form="♂ (male)"]
  J7 = male pin header, 4 pins [form="♂ (male)"]
  J8 = male pin header, 2 pins [form="♂ (male)"]
  buz2 = Piezo Buzzer
  R3 = Resistor [tolerance=±5% resistance=220 package=THT]
  R4 = Resistor [tolerance=±5% resistance=220 package=THT]
  LED2 = LED - 5mm [color="Red (633nm)" package="5 mm [THT]"]
  U1 = Optocoupler [package=THT]

nets:
  N1: C2.0, J6.pin1, J8.pin1, U1.Pin_2
  N2: C2.1, J6.pin2, J8.pin2, R4.Pin_0
  N3: J7.pin3, U1.Pin_4
  N4: J7.pin4, buz2.pin_1, LED2.anode
  N5: buz2.pin_2, R3.Pin_1, U1.Pin_5
  N6: R3.Pin_0, LED2.cathode
  N7: R4.Pin_1, U1.Pin_1

notes:
  +
  +5V
  -

custom parts:
  Piezo Buzzer: Part from https://www.nutsvolts.com/magazine/article/november2012_SmileysWorkshop. Breadboard and icon images modified to be 0.3" in spacing and be more similar to the actual physical part.
