# Fritzing sketch HDD-Clicker-Mark-03 (saved by Fritzing 0.9.3b)
breadboards: 1

parts:
  C3 = Ceramic Capacitor [capacitance=100nF package="100 mil [THT, multilayer]"]
  J9 = male pin header, 2 pins [form="♂ (male)"]
  J10 = male pin header, 2 pins [form="♂ (male)"]
  J11 = male pin header, 4 pins [form="♂ (male)"]
  buz3 = Piezo Buzzer
  R5 = Resistor [tolerance=±5% resistance=220 package=THT]
  LED3 = LED - 5mm [color="Red (633nm)" package="5 mm [THT]"]
  U2 = Optocoupler [package=THT]
  R6 = Resistor [tolerance=±5% resistance=220 package=THT]
  IC1 = IC, DIP package, 14 pins [chip_label=CD4047]
  R7 = Resistor [tolerance=±5% resistance=10k package=THT]
  C4 = Ceramic Capacitor [capacitance=100nF package="100 mil [THT, multilayer]"]
  R8 = Resistor [tolerance=±5% resistance=100k package=THT]
  VR1 = Trimpot-#3296-flat [package=3386u]
  JS1 = Generic Jumper Shunt

nets:
  N1: C3.0, J9.pin1, J10.pin1, JS1.pin2
  N2: C3.1, J9.pin2, J10.pin2, R6.Pin_0
  N3: J11.pin3, buz3.pin_2, LED3.cathode, IC1.pin5, IC1.pin6, IC1.pin7, IC1.pin9, IC1.pin12, R7.Pin_1
  N4: J11.pin4, U2.Pin_5, IC1.pin4, IC1.pin14
  N5: buz3.pin_1, R5.Pin_1, IC1.pin10
  N6: R5.Pin_0, LED3.anode
  N7: U2.Pin_1, R6.Pin_1
  N8: U2.Pin_2, JS1.pin1
  N9: U2.Pin_4, IC1.pin8, R7.Pin_0
  N10: IC1.pin1, C4.1
  N11: IC1.pin2, VR1.WIPER
  N12: IC1.pin3, C4.0, R8.Pin_1
  N13: R8.Pin_0, VR1.CW

notes:
  +
  -
  +5V
  Adjust sound
  with this
  100K Pot

custom parts:
  Piezo Buzzer: Part from https://www.nutsvolts.com/magazine/article/november2012_SmileysWorkshop. Breadboard and icon images modified to be 0.3" in spacing and be more similar to the actual physical part.
  Trimpot-#3296-flat: Bourns #3296 Square Trimpot 25 turn lying flat for low profile
